# Fritzing sketch load cell schematic (saved by Fritzing 0.9.10b)
breadboards: 1

parts:
  Part1 = HX711 Weighing Sensor Module
  Part3 = Arduino Uno (Rev3) - ICSP
  microSD1 = MicroSD Card Module
  U1 = MCP73831 [package=sot23-5]  # not connected

nets:
  VCC: Part1.VCC, Part3.3V3
  GND: Part1.GND, Part3.GND, microSD1.GND
  N1: Part1.DO/RX, Part3.D2
  N2: Part1.CK/TX, Part3.D1/TX
  N3: Part3.ICSP_MISO, Part3.D12/MISO, microSD1.MISO
  N4: Part3.D11_PWM/MOSI, microSD1.MOSI
  N5: Part3.D13/SCK, microSD1.SCK
  N6: Part3.D4, microSD1.CS
  5V: Part3.5V, microSD1.VCC
